# Fritzing sketch dc-bt (saved by Fritzing 0.9.0b)
breadboards: 1

parts:
  KT815 = NPN-Transistor [package="TO92 [THT]"]
  R1 = Resistor [tolerance=±5% resistance=360 package=THT]
  MDC = DC Motor
  VCC1 = Battery block 9V
  BT1 = Bluetooth HC-06u [package=THT]
  Digispark1 = Digispark
  D1 = Rectifier Diode [part_number=1N4007 package="300 mil [THT]"]

nets:
  GND: KT815.E, VCC1.-, BT1.GND, Digispark1.GND
  N1: KT815.B, R1.Pin_0
  N2: KT815.C, MDC.pin_2, D1.anode
  N3: R1.Pin_1, Digispark1.P1
  N4: MDC.pin_1, VCC1.+, Digispark1.VIN, D1.cathode
  VCC: BT1.VCC, Digispark1.VCC
  N5: BT1.TXD, Digispark1.P2
  N6: BT1.RXD, Digispark1.P3

custom parts:
  Bluetooth HC-06u: Bluetooth HC-06 - face up, pins down 16.5mm x 37.5mm PCB
  Digispark: The Digispark is an Attiny85 based microcontroller development board similar to the Arduino line, only cheaper, smaller, and a bit less powerful. With a whole host of shields to extend its functionality and the ability to use the familiar Arduino IDE the Digispark is a great way to jump into electronics, or perfect for when an Arduino is too big or too much.
